# Fritzing sketch CARRIERELEC (saved by Fritzing 0.8.3b)
circuit board: 5.79431cm x 8.67559cm
breadboards: 1

parts:
  Arduino1 = Arduino
  Main_Power_Solenoid = Relay [part_number=FRS1B-S package=THT]
  VCC1 = Battery
  S1 = Pushbutton [package=THT]
  TO_UBEC = Screw terminal - 2 pins [package=THT]
  FROM_SUBMINI_X1 = Screw terminal - 2 pins [package=THT]
  R1 = Resistor [tolerance=±5% resistance=220 package=THT]
  R2 = Resistor [tolerance=±5% resistance=220 package=THT]
  TO_LV_BOARD = Screw terminal - 2 pins [package=THT]
  Master_Fuse_80A = Fuse with Handler [part_number=Htc-15m]
  10k = Resistor [tolerance=±5% resistance=10k package=THT]
  10k_2 = Resistor [tolerance=±5% resistance=10k package=THT]
  C1 = Ceramic Capacitor [capacitance=0.1µF package="100 mil [THT, multilayer]"]
  C2 = Ceramic Capacitor [capacitance=0.1µF package="100 mil [THT, multilayer]"]
  E_Stop = Pushbutton [package=THT]
  VCC2 = Battery
  M1 = DC Motor
  M2 = DC Motor
  S2 = Pushbutton [package=THT]
  TO_SABRE = Screw terminal - 2 pins [package=THT]
  A1_A2_A3_A4_A5 = screw terminal, 5 pins
  RADIO_IN = screw terminal, 5 pins
  13_12_9_8_7 = screw terminal, 5 pins
  5V_GND = screw terminal, 2 pins
  MOTOR = screw terminal, 3 pins
  24V_IN = screw terminal, 2 pins
  RST_GND = screw terminal, 2 pins
  SERIAL = screw terminal, 2 pins
  I2C = screw terminal, 2 pins

nets:
  N1: Arduino1.GND, R2.Pin_1, C1.0, C2.0, 5V_GND.pin2, MOTOR.pin1, 24V_IN.pin2, RST_GND.pin2
  N2: Arduino1.D13, 13_12_9_8_7.pin1
  N3: Arduino1.D12, 13_12_9_8_7.pin2
  N4: Arduino1.D11, 10k.Pin_1
  N5: Arduino1.D10, 10k_2.Pin_1
  N6: Arduino1.D9, 13_12_9_8_7.pin3
  N7: Arduino1.D8, 13_12_9_8_7.pin4
  N8: Arduino1.D7, 13_12_9_8_7.pin5
  N9: Arduino1.D6, RADIO_IN.pin1
  N10: Arduino1.D5, RADIO_IN.pin2
  N11: Arduino1.D4, RADIO_IN.pin3
  N12: Arduino1.D3, RADIO_IN.pin4
  N13: Arduino1.D2, RADIO_IN.pin5
  N14: Arduino1.D1TX, SERIAL.pin1
  N15: Arduino1.D0RX, SERIAL.pin2
  N16: Arduino1.RST, RST_GND.pin1
  N17: Arduino1.VIN, 5V_GND.pin1
  N18: Arduino1.A0, R1.Pin_0, R2.Pin_0
  N19: Arduino1.A1, A1_A2_A3_A4_A5.pin1
  N20: Arduino1.A2, A1_A2_A3_A4_A5.pin2
  N21: Arduino1.A3, A1_A2_A3_A4_A5.pin3
  N22: Arduino1.A4, A1_A2_A3_A4_A5.pin4
  N23: Arduino1.A5, A1_A2_A3_A4_A5.pin5
  N24: Arduino1.SCL, I2C.pin1
  N25: Arduino1.SDA, I2C.pin2
  N26: Main_Power_Solenoid.COIL1, FROM_SUBMINI_X1.pin1
  N27: Main_Power_Solenoid.C1, Main_Power_Solenoid.C2, S1.leg1, Master_Fuse_80A.Connector2
  N28: Main_Power_Solenoid.COIL2, VCC1.-, TO_UBEC.pin2, FROM_SUBMINI_X1.pin2, TO_LV_BOARD.pin2, TO_SABRE.pin2
  N29: VCC1.+, Master_Fuse_80A.Connector1
  N30: S1.leg0, E_Stop.leg1
  N31: TO_UBEC.pin1, TO_LV_BOARD.pin1, E_Stop.leg0, TO_SABRE.pin1
  N32: R1.Pin_1, 24V_IN.pin1
  N33: 10k.Pin_0, C1.1, MOTOR.pin2
  N34: 10k_2.Pin_0, C2.1, MOTOR.pin3
  N35: VCC2.-, M1.pin_1, M2.pin_2
  N36: VCC2.+, S2.leg1
  N37: M1.pin_2, M2.pin_1, S2.leg0

notes:
  SCL SDA
  0v 11 10
  TX RX
  + -
