# Fritzing sketch electronics 1 (saved by Fritzing 0.7.9b)
perfboards: 1

parts:
  Q1 = Basic FET P-Channel [package="TO220 [THT]"]
  Q2 = Basic FET P-Channel [package="TO220 [THT]"]
  Q3 = Basic FET P-Channel [package="TO220 [THT]"]
  Q4 = Basic FET P-Channel [package="TO220 [THT]"]
  Q5 = Basic FET P-Channel [package="TO220 [THT]"]
  Q6 = Basic FET P-Channel [package="TO220 [THT]"]
  Q7 = Basic FET P-Channel [package="TO220 [THT]"]
  Q8 = Basic FET P-Channel [package="TO220 [THT]"]
  Q9 = Basic FET P-Channel [package="TO220 [THT]"]
  Q10 = Basic FET P-Channel [package="TO220 [THT]"]
  Q11 = Basic FET P-Channel [package="TO220 [THT]"]
  Q12 = Basic FET P-Channel [package="TO220 [THT]"]
  M1 = DC Motor
  Arduino1 = Arduino
  DC_Power1 = DC Power [voltage=5]
  part = Pad [width=7.90222222222222 height=9.03111111111111 connect=center]  # not connected
  K1 = Relay [part_number=FRS1B-S package=THT]
  Q13 = Basic FET P-Channel [package="TO220 [THT]"]
  Q14 = Basic FET P-Channel [package="TO220 [THT]"]
  Q15 = Basic FET P-Channel [package="TO220 [THT]"]
  Q16 = Basic FET P-Channel [package="TO220 [THT]"]
  Q17 = Basic FET P-Channel [package="TO220 [THT]"]
  Q18 = Basic FET P-Channel [package="TO220 [THT]"]
  Q19 = Basic FET P-Channel [package="TO220 [THT]"]
  Q20 = Basic FET P-Channel [package="TO220 [THT]"]
  Q21 = Basic FET P-Channel [package="TO220 [THT]"]
  Q22 = Basic FET P-Channel [package="TO220 [THT]"]
  Q23 = Basic FET P-Channel [package="TO220 [THT]"]
  Q24 = Basic FET P-Channel [package="TO220 [THT]"]
  M2 = DC Motor
  U1 = Arduino Mega  # not connected

nets:
  N1: Q1.gate, Q2.gate, Q3.gate, Arduino1.D10
  N2: Q1.drain, Q2.drain, Q3.drain, Q4.drain, Q5.drain, Q6.drain, K1.B, Q13.drain, Q14.drain, Q15.drain, Q17.drain, Q20.drain, Q24.drain
  N3: Q1.source, Q2.source, Q3.source, Q7.drain, Q8.drain, Q9.drain, M1.pin_1
  N4: Q4.gate, Q5.gate, Q6.gate, Arduino1.D11
  N5: Q4.source, Q5.source, Q6.source, Q10.drain, Q11.drain, Q12.drain, M1.pin_2
  N6: Q7.gate, Q8.gate, Q9.gate, Arduino1.D9
  GND: Q7.source, Q8.source, Q9.source, Q10.source, Q11.source, Q12.source, Arduino1.GND, DC_Power1.GND, K1.COIL1, Q16.source, Q18.source, Q19.source, Q21.source, Q22.source, Q23.source
  N7: Q10.gate, Q11.gate, Q12.gate, Arduino1.D8
  N8: Arduino1.D12, K1.COIL2
  N9: Arduino1.D6, Q13.gate, Q14.gate, Q20.gate
  N10: Arduino1.D5, Q15.gate, Q17.gate, Q24.gate
  N11: Arduino1.D4, Q16.gate, Q18.gate, Q21.gate
  N12: Arduino1.D3, Q19.gate, Q22.gate, Q23.gate
  N13: DC_Power1.V+, K1.C1
  N14: Q13.source, Q14.source, Q19.drain, Q20.source, Q22.drain, Q23.drain, M2.pin_2
  N15: Q15.source, Q16.drain, Q17.source, Q18.drain, Q21.drain, Q24.source, M2.pin_1
